// Logisim project TBX32.circ as structural Verilog: 5 circuits, main circuit main
module main (
);

  wire undriven_5, undriven_6;
  wire [4:0] undriven_2, undriven_3, undriven_4;
  wire [31:0] alu_1_output, registerbank_1_output__1, registerbank_1_output__2, undriven;

  // Probe on undriven_2
  // Probe on undriven_3
  // Probe on undriven
  // Probe on undriven_4
  RegisterBank registerbank_1 (
    .Data(undriven), .Write_Selector(undriven_4), .Write_Enable(undriven_5),
    .Output__1(registerbank_1_output__1), .Output__2(registerbank_1_output__2),
    .Read__1_Selector(undriven_2), .Clock(undriven_6), .Read__2_Selector(undriven_3));
  // Probe on registerbank_1_output__1
  // Probe on registerbank_1_output__2
  ALU alu_1 (
    .Input__1(registerbank_1_output__1), .Input__2(registerbank_1_output__2), .Output(alu_1_output));  // open: Flags, ALUadd, ALUsub, ALUmul, ALUdiv, ALUmod, ALUneg, ALUand, ALUor, ALUxor, ALUshl, ALUshr, ALUcmp
endmodule

module RegisterBank (
  input  [4:0] Read__1_Selector,
  input  [31:0] Data,
  input  [4:0] Write_Selector,
  input  Write_Enable,
  input  Clock,
  input  [4:0] Read__2_Selector,
  output [31:0] Output__1,
  output [31:0] Output__2
);

  wire decoder_1_out0, decoder_1_out1, decoder_1_out2, decoder_1_out3, decoder_1_out4, decoder_1_out5,
       decoder_1_out6, decoder_1_out7, decoder_1_out8, decoder_1_out9, decoder_1_out10, decoder_1_out11,
       decoder_1_out12, decoder_1_out13, decoder_1_out14, decoder_1_out15, decoder_1_out16, decoder_1_out17,
       decoder_1_out18, decoder_1_out19, decoder_1_out20, decoder_1_out21, decoder_1_out22, decoder_1_out23,
       decoder_1_out24, decoder_1_out25, decoder_1_out26, decoder_1_out27, decoder_1_out28, decoder_1_out29,
       decoder_1_out30, decoder_1_out31;
  wire [31:0] R00out, R01out, R02out, R03out, R04out, R05out, R06out, R07out, R08out, R09out, R10out, R11out,
       R12out, R13out, R14out, R15out, R16out, R17out, R18out, R19out, R20out, R21out, R22out, R23out,
       R24out, R25out, R26out, R27out, R28out, R29out, R30out, R31out;

  // Probe on decoder_1_out0
  Register #(.width(32)) register_1 (.D(Data), .en(decoder_1_out0), .Q(R00out), .clk(Clock));  // open: clr
  Register #(.width(32)) register_2 (.D(Data), .en(decoder_1_out1), .Q(R01out), .clk(Clock));  // open: clr
  Register #(.width(32)) register_3 (.D(Data), .en(decoder_1_out2), .Q(R02out), .clk(Clock));  // open: clr
  Register #(.width(32)) register_4 (.D(Data), .en(decoder_1_out3), .Q(R03out), .clk(Clock));  // open: clr
  Register #(.width(32)) register_5 (.D(Data), .en(decoder_1_out4), .Q(R04out), .clk(Clock));  // open: clr
  Register #(.width(32)) register_6 (.D(Data), .en(decoder_1_out5), .Q(R05out), .clk(Clock));  // open: clr
  Register #(.width(32)) register_7 (.D(Data), .en(decoder_1_out6), .Q(R06out), .clk(Clock));  // open: clr
  Register #(.width(32)) register_8 (.D(Data), .en(decoder_1_out7), .Q(R07out), .clk(Clock));  // open: clr
  // Probe on Write_Selector
  Decoder #(.select(5), .disabled(0)) decoder_1 (
    .out0(decoder_1_out0), .out1(decoder_1_out1), .out2(decoder_1_out2), .out3(decoder_1_out3),
    .out4(decoder_1_out4), .out5(decoder_1_out5), .out6(decoder_1_out6), .out7(decoder_1_out7),
    .out8(decoder_1_out8), .out9(decoder_1_out9), .out10(decoder_1_out10), .out11(decoder_1_out11),
    .out12(decoder_1_out12), .out13(decoder_1_out13), .out14(decoder_1_out14), .out15(decoder_1_out15),
    .out16(decoder_1_out16), .out17(decoder_1_out17), .out18(decoder_1_out18), .out19(decoder_1_out19),
    .out20(decoder_1_out20), .out21(decoder_1_out21), .out22(decoder_1_out22), .out23(decoder_1_out23),
    .out24(decoder_1_out24), .out25(decoder_1_out25), .out26(decoder_1_out26), .out27(decoder_1_out27),
    .out28(decoder_1_out28), .out29(decoder_1_out29), .out30(decoder_1_out30), .out31(decoder_1_out31),
    .sel(Write_Selector), .en(Write_Enable));
  Register #(.width(32)) register_9 (.D(Data), .en(decoder_1_out8), .Q(R08out), .clk(Clock));  // open: clr
  Register #(.width(32)) register_10 (.D(Data), .en(decoder_1_out9), .Q(R09out), .clk(Clock));  // open: clr
  Register #(.width(32)) register_11 (.D(Data), .en(decoder_1_out10), .Q(R10out), .clk(Clock));  // open: clr
  Register #(.width(32)) register_12 (.D(Data), .en(decoder_1_out11), .Q(R11out), .clk(Clock));  // open: clr
  Register #(.width(32)) register_13 (.D(Data), .en(decoder_1_out12), .Q(R12out), .clk(Clock));  // open: clr
  Register #(.width(32)) register_14 (.D(Data), .en(decoder_1_out13), .Q(R13out), .clk(Clock));  // open: clr
  Register #(.width(32)) register_15 (.D(Data), .en(decoder_1_out14), .Q(R14out), .clk(Clock));  // open: clr
  Register #(.width(32)) register_16 (.D(Data), .en(decoder_1_out15), .Q(R15out), .clk(Clock));  // open: clr
  Register #(.width(32)) register_17 (.D(Data), .en(decoder_1_out16), .Q(R16out), .clk(Clock));  // open: clr
  Register #(.width(32)) register_18 (.D(Data), .en(decoder_1_out17), .Q(R17out), .clk(Clock));  // open: clr
  Register #(.width(32)) register_19 (.D(Data), .en(decoder_1_out18), .Q(R18out), .clk(Clock));  // open: clr
  Register #(.width(32)) register_20 (.D(Data), .en(decoder_1_out19), .Q(R19out), .clk(Clock));  // open: clr
  Register #(.width(32)) register_21 (.D(Data), .en(decoder_1_out20), .Q(R20out), .clk(Clock));  // open: clr
  Register #(.width(32)) register_22 (.D(Data), .en(decoder_1_out21), .Q(R21out), .clk(Clock));  // open: clr
  Register #(.width(32)) register_23 (.D(Data), .en(decoder_1_out22), .Q(R22out), .clk(Clock));  // open: clr
  Register #(.width(32)) register_24 (.D(Data), .en(decoder_1_out23), .Q(R23out), .clk(Clock));  // open: clr
  Register #(.width(32)) register_25 (.D(Data), .en(decoder_1_out24), .Q(R24out), .clk(Clock));  // open: clr
  Register #(.width(32)) register_26 (.D(Data), .en(decoder_1_out25), .Q(R25out), .clk(Clock));  // open: clr
  Register #(.width(32)) register_27 (.D(Data), .en(decoder_1_out26), .Q(R26out), .clk(Clock));  // open: clr
  Register #(.width(32)) register_28 (.D(Data), .en(decoder_1_out27), .Q(R27out), .clk(Clock));  // open: clr
  Register #(.width(32)) register_29 (.D(Data), .en(decoder_1_out28), .Q(R28out), .clk(Clock));  // open: clr
  Register #(.width(32)) register_30 (.D(Data), .en(decoder_1_out29), .Q(R29out), .clk(Clock));  // open: clr
  Register #(.width(32)) register_31 (.D(Data), .en(decoder_1_out30), .Q(R30out), .clk(Clock));  // open: clr
  Register #(.width(32)) register_32 (.D(Data), .en(decoder_1_out31), .Q(R31out), .clk(Clock));  // open: clr
  Multiplexer #(.select(5), .width(32), .enable("false")) multiplexer_1 (
    .in0(R00out), .in1(R01out), .in2(R02out), .in3(R03out), .in4(R04out), .in5(R05out), .in6(R06out),
    .in7(R07out), .in8(R08out), .in9(R09out), .in10(R10out), .in11(R11out), .in12(R12out), .in13(R13out),
    .in14(R14out), .in15(R15out), .in16(R16out), .in17(R17out), .in18(R18out), .in19(R19out), .in20(R20out),
    .in21(R21out), .in22(R22out), .in23(R23out), .in24(R24out), .in25(R25out), .in26(R26out), .in27(R27out),
    .in28(R28out), .in29(R29out), .in30(R30out), .in31(R31out), .out(Output__1), .sel(Read__1_Selector));
  Multiplexer #(.select(5), .width(32), .enable("false")) multiplexer_2 (
    .in0(R00out), .in1(R01out), .in2(R02out), .in3(R03out), .in4(R04out), .in5(R05out), .in6(R06out),
    .in7(R07out), .in8(R08out), .in9(R09out), .in10(R10out), .in11(R11out), .in12(R12out), .in13(R13out),
    .in14(R14out), .in15(R15out), .in16(R16out), .in17(R17out), .in18(R18out), .in19(R19out), .in20(R20out),
    .in21(R21out), .in22(R22out), .in23(R23out), .in24(R24out), .in25(R25out), .in26(R26out), .in27(R27out),
    .in28(R28out), .in29(R29out), .in30(R30out), .in31(R31out), .out(Output__2), .sel(Read__2_Selector));
endmodule

module ALU (
  input  ALUadd,
  input  ALUmul,
  input  ALUmod,
  input  ALUand,
  input  ALUxor,
  input  ALUshr,
  input  [31:0] Input__1,
  input  ALUsub,
  input  ALUdiv,
  input  ALUneg,
  input  ALUor,
  input  ALUshl,
  input  ALUcmp,
  input  [31:0] Input__2,
  output [31:0] Output,
  output [31:0] Flags
);

  wire CarryFlag, comparator_1_eq, comparator_1_gt, comparator_1_lt, EqualFlag, NegativeFlag, not_1_out,
       or_2_out, OverflowFlag, PositiveFlag, ZeroFlag;
  wire [31:0] addsubber_1_q, and_1_out, divider_1_out, divider_1_rem, multiplier_1_out, negator_1_out,
       or_1_out, shifter_1_out, shifter_2_out, xor_1_out;

  AddSubber addsubber_1 (
    .D1(Input__1), .D2(Input__2), .Q(addsubber_1_q), .Add(ALUadd), .Sub(ALUsub), .Cout(CarryFlag),
    .Overflow(OverflowFlag));
  Multiplier #(.width(32)) multiplier_1 (.a(Input__1), .b(Input__2), .out(multiplier_1_out));  // open: cin, cout
  Divider #(.width(32)) divider_1 (
    .a(Input__1), .b(Input__2), .out(divider_1_out), .rem(divider_1_rem));  // open: upper
  Negator #(.width(32)) negator_1 (.in(Input__1), .out(negator_1_out));
  assign and_1_out = Input__1 & Input__2;  // AND_Gate and_1, 32 bits wide
  assign or_1_out = Input__1 | Input__2;  // OR_Gate or_1, 32 bits wide
  assign xor_1_out = Input__1 ^ Input__2;  // XOR_Gate xor_1, 32 bits wide
  Shifter #(.width(32)) shifter_1 (.in(Input__1), .\dist (Input__2[4:0]), .out(shifter_1_out));
  Shifter #(.width(32), .shift("lr")) shifter_2 (.in(Input__1), .\dist (Input__2[4:0]), .out(shifter_2_out));
  Comparator #(.width(32)) comparator_1 (
    .a(Input__1), .b(Input__2), .gt(comparator_1_gt), .eq(comparator_1_eq), .lt(comparator_1_lt));
  not not_1 (not_1_out, ALUcmp);
  assign EqualFlag = not_1_out ? 1'b0 : 1'bz;  // Controlled_Buffer controlled_buffer_1
  or or_2 (or_2_out, ALUadd, ALUsub);
  assign Output = or_2_out ? addsubber_1_q : 32'bz;  // Controlled_Buffer controlled_buffer_2
  assign Output = ALUmul ? multiplier_1_out : 32'bz;  // Controlled_Buffer controlled_buffer_3
  assign EqualFlag = ALUcmp ? comparator_1_gt : 1'bz;  // Controlled_Buffer controlled_buffer_4
  assign EqualFlag = ALUcmp ? comparator_1_eq : 1'bz;  // Controlled_Buffer controlled_buffer_5
  assign Output = ALUdiv ? divider_1_out : 32'bz;  // Controlled_Buffer controlled_buffer_6
  assign Output = ALUmod ? divider_1_rem : 32'bz;  // Controlled_Buffer controlled_buffer_7
  assign EqualFlag = ALUcmp ? comparator_1_lt : 1'bz;  // Controlled_Buffer controlled_buffer_8
  assign Output = ALUneg ? negator_1_out : 32'bz;  // Controlled_Buffer controlled_buffer_9
  assign Output = ALUand ? and_1_out : 32'bz;  // Controlled_Buffer controlled_buffer_10
  assign Output = ALUor ? or_1_out : 32'bz;  // Controlled_Buffer controlled_buffer_11
  assign Output = ALUxor ? xor_1_out : 32'bz;  // Controlled_Buffer controlled_buffer_12
  assign Output = ALUshl ? shifter_1_out : 32'bz;  // Controlled_Buffer controlled_buffer_13
  assign Output = ALUshr ? shifter_2_out : 32'bz;  // Controlled_Buffer controlled_buffer_14
  Comparator #(.width(32)) comparator_2 (
    .a(Output), .b({32{1'b0}}), .gt(PositiveFlag), .eq(ZeroFlag), .lt(NegativeFlag));
  assign Flags = {{24{1'b0}}, {{3{EqualFlag}}, OverflowFlag, NegativeFlag, ZeroFlag, PositiveFlag, CarryFlag}};  // Bit_Extender bit_extender_1

  // Other names for the same wires on the sheet: GreaterFlag = EqualFlag; LessFlag = EqualFlag
endmodule

module AddSubber (
  input  Add,
  input  Sub,
  input  [31:0] D1,
  input  [31:0] D2,
  output [31:0] Q,
  output Cout,
  output Overflow
);

  wire adder_1_cout, and_1_out, and_2_out, bitselector_1_out, bitselector_2_out, bitselector_3_out,
       multiplexer_1_out, multiplexer_2_out, not_1_out, not_2_out, not_3_out, not_4_out, not_5_out,
       subtractor_1_bout;
  wire [31:0] adder_1_out, subtractor_1_out;

  BitSelector #(.width(32)) bitselector_1 (.in(D2), .out(bitselector_1_out), .sel({5{1'b1}}));
  BitSelector #(.width(32)) bitselector_2 (.in(D1), .out(bitselector_2_out), .sel({5{1'b1}}));
  BitSelector #(.width(32)) bitselector_3 (.in(Q), .out(bitselector_3_out), .sel({5{1'b1}}));
  Adder #(.width(32)) adder_1 (.a(D1), .b(D2), .out(adder_1_out), .cout(adder_1_cout));  // open: cin
  Subtractor #(.width(32)) subtractor_1 (
    .a(D1), .b(D2), .out(subtractor_1_out), .bout(subtractor_1_bout));  // open: bin
  not not_1 (not_1_out, bitselector_3_out);
  not not_2 (not_2_out, bitselector_2_out);
  not not_3 (not_3_out, bitselector_1_out);
  assign Q = Add ? adder_1_out : 32'bz;  // Controlled_Buffer controlled_buffer_1
  not not_4 (not_4_out, Add);
  Multiplexer #(.disabled(0), .enable("false")) multiplexer_1 (
    .in0(adder_1_cout), .in1(1'b0), .out(multiplexer_1_out), .sel(not_4_out));
  assign Q = Sub ? subtractor_1_out : 32'bz;  // Controlled_Buffer controlled_buffer_2
  not not_5 (not_5_out, Sub);
  Multiplexer #(.disabled(0), .enable("false")) multiplexer_2 (
    .in0(subtractor_1_bout), .in1(1'b0), .out(multiplexer_2_out), .sel(not_5_out));
  or or_1 (Cout, multiplexer_1_out, multiplexer_2_out);
  and and_1 (and_1_out, not_1_out, bitselector_2_out, bitselector_1_out);
  and and_2 (and_2_out, bitselector_3_out, not_2_out, not_3_out);
  or or_2 (Overflow, and_1_out, and_2_out);
endmodule

module ControlUnit (
  input  [4:0] OpCode
);

  wire clock_1_out, not_1_out;
  wire [7:0] counter_1_q, rom_1_data, rom_2_data;

  Clock clock_1 (.out(clock_1_out));
  ROM #(.addrWidth(5)) rom_1 (.addr(OpCode), .data(rom_1_data));  // open: sel
  // Probe on rom_1_data
  Counter counter_1 (
    .load(rom_2_data[1]), .D(rom_1_data), .count(not_1_out), .Q(counter_1_q), .clk(clock_1_out),
    .clr(rom_2_data[3]));  // open: carry
  not not_1 (not_1_out, rom_2_data[1]);
  ROM rom_2 (.addr(counter_1_q), .data(rom_2_data));  // open: sel

  // Notes on the sheet:
  //   contents of rom_1 (hex, n*v repeats v):
  //   1 2 3 4 5 6 7 8 8*0 a b c d e f 1f 2f 3f 4f 5f 6f 7f 8f 9f af
  //   contents of rom_2 (hex, n*v repeats v):
  //   1 2 3 4 5 0 0 8 8*0 a b c d e f 1f 2f 3f 4f 5f 6f 7f 8f 9f af
endmodule
